# Fritzing sketch piezoDrum (saved by Fritzing 0.9.3b)
breadboards: 1

parts:
  Componente1 = Arduino Uno (Rev3)
  J1 = Piezo Speaker
  J2 = Piezo Speaker
  J3 = Piezo Speaker
  R1 = Resistor [tolerance=±5% resistance=1M package=THT]
  R2 = Resistor [tolerance=±5% resistance=1M package=THT]
  R3 = Resistor [tolerance=±5% resistance=1M package=THT]

nets:
  N1: Componente1.A0, J1.pin2, R1.Pin_1
  N2: Componente1.A1, J2.pin2, R2.Pin_1
  N3: Componente1.A2, J3.pin2, R3.Pin_1
  N4: Componente1.GND, J1.pin1, J2.pin1, J3.pin1, R1.Pin_0, R2.Pin_0, R3.Pin_0
